# Fritzing sketch Demonstration Device (saved by Fritzing 0.9.3b)
breadboards: 1

parts:
  Bauteil1 = Arduino Pro Mini (3.3V)
  U1 = mystery part, 6 pins [chip_label=HC-05]
  LED1 = LED - 5mm [color="Yellow (592nm)" package="5 mm [THT]"]
  R1 = Resistor [tolerance=±5% resistance=220 package=THT]
  U2 = SWITCH-SPST-2 [package=switch-spst-vertical]
  U3 = SWITCH-SPST-2 [package=switch-spst-vertical]
  S1 = Round Pushbutton
  R2 = Resistor [tolerance=±5% resistance=220 package="0402 [SMD]"]
  Bauteil2 = Adafruit Ultimate GPS v3 [part_number="Adafruit #746"]
  DHT1 = DHT11 Humitidy and Temperature Sensor
  R4 = Resistor [tolerance=±5% resistance=4.7k package=THT]
  LED3 = LED - 5mm [color="Green (565nm)" package="5 mm [THT]"]
  LED4 = LED - 5mm [color="Red (633nm)" package="5 mm [THT]"]
  R5 = Resistor [tolerance=±5% resistance=220 package=THT]
  BATT1 = 4xAA Switchable Battery Pack w/JST connector
  DS1 = DS18B20 1-Wire Temperature Sensor [part_number=DS18B20]
  R3 = Resistor [tolerance=±5% resistance=4.7k package=THT]

nets (from the schematic view):
  GND: Bauteil1.GND, U1.pin4, R1.Pin_1, S1.leg1, R2.Pin_1, Bauteil2.GND, DHT1.GND, R5.Pin_1, BATT1.NEG, DS1.GND
  N1: Bauteil1.RAW, U2.O
  VDD: Bauteil1.VCC, U1.pin5, U3.P, DHT1.VDD, R4.Pin_1, DS1.VDD, R3.Pin_0
  N2: Bauteil1.A2, LED4.anode
  N3: Bauteil1.A1, LED3.anode
  N4: Bauteil1.MISO, DHT1.DATA, R4.Pin_0
  N5: Bauteil1.MOSI, Bauteil2.TX
  N6: Bauteil1.D10, Bauteil2.RX
  N7: Bauteil1.D9, DS1.DQ, R3.Pin_1
  N8: Bauteil1.D2, S1.leg0
  N9: Bauteil1.RXI, U1.pin3
  N10: Bauteil1.TXO, U1.pin2
  N11: U1.pin1, LED1.anode
  N12: LED1.cathode, R1.Pin_0
  N13: U2.P, BATT1.POS
  N14: U3.O, Bauteil2.VIN
  N15: R2.Pin_0, LED4.cathode
  N16: LED3.cathode, R5.Pin_0

custom parts:
  Adafruit Ultimate GPS v3: We carry a few different GPS modules here in the Adafruit shop, but none that satisfied our every desire - that's why we designed this little GPS breakout board. We believe this is the Ultimate GPS module, so we named it that. It's got everything you want and more: -165 dBm sensitivity, 10 Hz updates, 66 channels 5V friendly design and only 20mA current draw Breadboard friendly + two mounting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
  DHT11 Humitidy and Temperature Sensor: DHT11 Humidity and Temperature Sensor
  4xAA Switchable Battery Pack w/JST connector: 4xAA Switchable Battery Pack with JST connector
