# Fritzing sketch Pro Mini (saved by Fritzing 0.9.3b)
breadboards: 1

parts:
  Bauteil1 = Arduino Pro Mini (3.3V)
  U1 = mystery part, 6 pins [chip_label=HC-05]
  LED1 = LED - 5mm [color="Green (560nm)" package="5 mm [THT]"]
  R1 = Resistor [tolerance=±5% resistance=220 package=THT]
  BATT1 = 4xAA Switchable Battery Pack w/JST connector
  U2 = SWITCH-SPST-2 [package=switch-spst-vertical]
  U3 = SWITCH-SPST-2 [package=switch-spst-vertical]
  S1 = Round Pushbutton
  LED2 = LED - 3mm [color="Red (633nm)" package="3 mm [THT]"]
  R2 = Resistor [tolerance=±5% resistance=220 package="0402 [SMD]"]
  Bauteil2 = Adafruit Ultimate GPS v3 [part_number="Adafruit #746"]

nets:
  GND: Bauteil1.GND, U1.pin4, R1.Pin_1, BATT1.NEG, S1.leg1, R2.Pin_1, Bauteil2.GND
  N1: Bauteil1.RAW, U2.O
  N2: Bauteil1.VCC, U1.pin5, U3.P
  N3: Bauteil1.A2, LED2.anode
  N4: Bauteil1.MOSI, Bauteil2.TX
  N5: Bauteil1.D10, Bauteil2.RX
  N6: Bauteil1.D2, S1.leg0
  N7: Bauteil1.RXI, U1.pin3
  N8: Bauteil1.TXO, U1.pin2
  N9: U1.pin1, LED1.anode
  N10: LED1.cathode, R1.Pin_0
  N11: BATT1.POS, U2.P
  N12: U3.O, Bauteil2.VIN
  N13: LED2.cathode, R2.Pin_0

custom parts:
  4xAA Switchable Battery Pack w/JST connector: 4xAA Switchable Battery Pack with JST connector
  Adafruit Ultimate GPS v3: We carry a few different GPS modules here in the Adafruit shop, but none that satisfied our every desire - that's why we designed this little GPS breakout board. We believe this is the Ultimate GPS module, so we named it that. It's got everything you want and more: -165 dBm sensitivity, 10 Hz updates, 66 channels 5V friendly design and only 20mA current draw Breadboard friendly + two mounting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
